# Fritzing sketch dht (saved by Fritzing 0.8.5b)
breadboards: 1

parts:
  Bauteil1 = Arduino Uno (Rev3)
  RHT1 = Humidity and Temperature Sensor RHT03
  R1 = Resistor [tolerance=±5% resistance=1k package=THT]

nets:
  N1: Bauteil1.GND, RHT1.GND_2
  N2: Bauteil1.D5_PWM, RHT1.Data-signal, R1.Pin_1
  5V: Bauteil1.5V, RHT1.Vcc, R1.Pin_0

notes:
  1kΩ Resistor
  DHT11
